// Logisim project circuit1a.circ as structural Verilog: 1 circuit, main circuit main
module main (
  input  A,
  input  B,
  input  C,
  output out
);

  wire and_1_out, and_2_out, not_1_out, or_1_out;

  and and_1 (and_1_out, B, ~C);  // AND_Gate
  and and_2 (and_2_out, A, B);
  not not_1 (not_1_out, and_2_out);
  or or_1 (or_1_out, and_1_out, C);
  or or_2 (out, not_1_out, or_1_out);

  // Notes on the sheet:
  //   Unefficient implementation of: (not(A and B)) or ((C) or (B and not C))
endmodule
