// Logisim project circuit1c.circ as structural Verilog: 1 circuit, main circuit main
module main (
  input  A,
  input  B,
  input  C,
  output out1,
  output out2
);

  wire and_1_out, and_2_out, and_3_out;

  and and_1 (and_1_out, ~A, B);  // AND_Gate
  and and_2 (and_2_out, ~B, C);  // AND_Gate
  and and_3 (and_3_out, A, B, ~C);  // AND_Gate
  or or_1 (out1, and_1_out, and_2_out, and_3_out);
  and and_4 (out2, B, ~C);  // AND_Gate
endmodule
