// Logisim project fsm.circ as structural Verilog: 1 circuit, main circuit main
module main (
  input  in1,
  input  in2,
  output out
);

  wire and_2_out, and_3_out, and_4_out, and_5_out, and_6_out, and_7_out, clk, or_1_out, or_2_out, Q0, Q1;

  Clock clock_1 (.out(clk));
  and and_1 (out, Q1, ~Q0);  // AND_Gate
  and and_2 (and_2_out, Q1, ~Q0, in1, ~in2);  // AND_Gate
  and and_3 (and_3_out, Q1, ~Q0, ~in1, in2);  // AND_Gate
  and and_4 (and_4_out, ~Q1, Q0, ~in1, in2);  // AND_Gate
  and and_5 (and_5_out, ~Q1, Q0, in1, ~in2);  // AND_Gate
  and and_6 (and_6_out, ~Q1, ~Q0, ~in1, in2);  // AND_Gate
  and and_7 (and_7_out, ~Q1, ~Q0, in1, ~in2);  // AND_Gate
  D_Flip_Flop f1 (.D(or_1_out), .clk(clk), .Q(Q1));  // open: Qn, preset, reset
  or or_1 (or_1_out, and_2_out, and_3_out, and_4_out, and_5_out);
  D_Flip_Flop f0 (.D(or_2_out), .clk(clk), .Q(Q0));  // open: Qn, preset, reset
  or or_2 (or_2_out, and_6_out, and_7_out);
endmodule
