// Logisim project hw4.circ as structural Verilog: 13 circuits, main circuit ALU
module main (
  input  reset
);

  wire ALU_Neg, ALU_Zero, ALUinB, and_1_out, and_2_out, beq, blt, clk, DMwe, IN, JP, keyboard_1_avail,
       memorylatch_1_oe_latched, memorylatch_1_we_latched, not_1_out, or_1_out, OUT, Rdst, RwD, Rwe;
  wire [2:0] ALUOp, multiplexer_1_out, multiplexer_2_out;
  wire [6:0] keyboard_1_data;
  wire [7:0] kboard_out;
  wire [11:0] Addr;
  wire [14:0] alu_3_outputdata;
  wire [15:0] alu_1_outputdata, alu_2_outputdata, memorylatch_1_address_latched,
       memorylatch_1_data_in_latched, multiplexer_3_out, multiplexer_4_out, multiplexer_6_out,
       multiplexer_7_out, multiplexer_8_out, ram_1_dout, register_1_output, RS1VAL, RS2VAL,
       signextender_1_output, signextender_2_output, twobitshifterleft_2_output;
  wire [15:12] InstructionMemory_data;

  not not_1 (not_1_out, clk);
  Clock u_clk (.out(clk));
  register register_1 (
    .WE(1'b1), .reset(reset), .dataInput(multiplexer_7_out), .\output (register_1_output), .clock(not_1_out));
  // Probe on register_1_output
  ALU alu_1 (
    .OpType(3'b000), .in1(register_1_output), .in2(16'h1), .OutputData(alu_1_outputdata));  // open: shamt, ovf, Zero
  ROM #(.addrWidth(16), .dataWidth(16)) InstructionMemory (
    .addr(register_1_output), .data({InstructionMemory_data, Addr}));
  // Probe on {InstructionMemory_data, Addr}
  signExtender signextender_1 (.\input (Addr[5:0]), .\output (signextender_1_output));
  // Probe on ALUOp
  instructionDecoder instructiondecoder_1 (
    .opcode(InstructionMemory_data), .Rwe(Rwe), .Rdst(Rdst), .ALUOp(ALUOp), .Rwd(RwD), .ALUinB(ALUinB),
    .DMwe(DMwe), .BEQ(beq), .BLT(blt), .JP(JP), .OUTPUT(OUT), .INPUT(IN));
  twoBitShifterLeft twobitshifterleft_1 (.\input (signextender_1_output), .bits(2'b10));  // open: output
  RegisterFile register_file (
    .WE(Rwe), .clk(clk), .reset(reset), .RDVAL(multiplexer_6_out), .RD(multiplexer_1_out), .RS1(Addr[11:9]),
    .RS2(Addr[8:6]), .RS1VAL(RS1VAL), .RS2VAL(RS2VAL));
  // Probe on Addr[11:9]
  // Probe on Addr[11:9]
  // Probe on signextender_1_output
  Multiplexer #(.width(3), .enable("false")) multiplexer_1 (
    .in0(multiplexer_2_out), .in1(3'b111), .out(multiplexer_1_out), .sel(JP));
  Multiplexer #(.width(3), .enable("false")) multiplexer_2 (
    .in0(Addr[8:6]), .in1(Addr[5:3]), .out(multiplexer_2_out), .sel(Rdst));
  // Probe on Addr[5:3]
  // Probe on Addr[8:6]
  // Probe on Addr[5:0]
  // Probe on Addr[8:6]
  ALU alu_2 (
    .OpType(3'b000), .in1(alu_1_outputdata), .in2(signextender_1_output), .OutputData(alu_2_outputdata));  // open: shamt, ovf, Zero
  // Probe on Addr[2:0]
  signExtender signextender_2 (.\input (Addr[5:0]), .\output (signextender_2_output));
  Keyboard keyboard_1 (.clk(clk), .re(IN), .clr(reset), .avail(keyboard_1_avail), .data(keyboard_1_data));
  and and_1 (and_1_out, beq, ALU_Zero);
  and and_2 (and_2_out, blt, ALU_Neg);
  Multiplexer #(.width(16), .enable("false")) multiplexer_3 (
    .in0(RS2VAL), .in1(signextender_2_output), .out(multiplexer_3_out), .sel(ALUinB));
  TTY #(.rows(13), .cols(80), .trigger("falling")) tty_1 (.data(RS1VAL[6:0]), .clk(clk), .we(OUT), .clr(reset));
  or or_1 (or_1_out, and_1_out, and_2_out);
  // Probe on RS1VAL
  // Probe on multiplexer_3_out
  // Probe on keyboard_1_data
  not not_2 (kboard_out[7], keyboard_1_avail);
  Multiplexer #(.width(16), .enable("false")) multiplexer_4 (
    .in0(alu_1_outputdata), .in1(alu_2_outputdata), .out(multiplexer_4_out), .sel(or_1_out));
  // Probe on multiplexer_6_out
  ALU alu_3 (
    .OpType(ALUOp), .in1(RS1VAL), .in2(multiplexer_3_out), .OutputData({ALU_Neg, alu_3_outputdata}),
    .shamt(Addr[2:0]), .Zero(ALU_Zero));  // open: ovf
  // Probe on {ALU_Neg, alu_3_outputdata}
  Multiplexer #(.width(7), .enable("false")) multiplexer_5 (
    .in0(keyboard_1_data), .in1({7{1'b0}}), .out(kboard_out[6:0]), .sel(kboard_out[7]));
  // Probe on {{8{1'b0}}, kboard_out}
  memoryLatch memorylatch_1 (
    .address({ALU_Neg, alu_3_outputdata}), .WE(DMwe), .clk(clk), .data_in(RS2VAL),
    .address_latched(memorylatch_1_address_latched), .WE_latched(memorylatch_1_we_latched),
    .OE_latched(memorylatch_1_oe_latched), .data_in_latched(memorylatch_1_data_in_latched));
  RAM #(.addrWidth(16), .dataWidth(16), .trigger("high"), .databus("bibus")) ram_1 (
    .addr(memorylatch_1_address_latched), .we(memorylatch_1_we_latched), .oe(memorylatch_1_oe_latched),
    .din(memorylatch_1_data_in_latched), .dout(ram_1_dout));
  twoBitShifterLeft twobitshifterleft_2 (
    .\input ({multiplexer_4_out[15:12], Addr}), .\output (twobitshifterleft_2_output), .bits(2'b10));
  Multiplexer #(.width(16), .enable("false")) multiplexer_6 (
    .in0(multiplexer_8_out), .in1({{8{1'b0}}, kboard_out}), .out(multiplexer_6_out), .sel(IN));
  Multiplexer #(.width(16), .enable("false")) multiplexer_7 (
    .in0(multiplexer_4_out), .in1({multiplexer_4_out[15:12], Addr}), .out(multiplexer_7_out), .sel(JP));
  Multiplexer #(.width(16), .enable("false")) multiplexer_8 (
    .in0({ALU_Neg, alu_3_outputdata}), .in1(ram_1_dout), .out(multiplexer_8_out), .sel(RwD));

  // Other names for the same wires on the sheet: Imm[5:0] = Addr[5:0]; Shamt[2:0] = Addr[2:0]; Rd[2:0] = Addr[5:3];
  //   Rt[2:0] = Addr[8:6]; Rs[2:0] = Addr[11:9]

  // Notes on the sheet:
  //   Program Counter
  //   contents of InstructionMemory (hex, n*v repeats v):
  //   6050 609f 7458 9050 909f 8458 203f
  //   R-Type
  //   I-Type
  //   J-Type
  //   Branch control
  //   Jump control
endmodule

module ALU (
  input  [2:0] OpType,
  input  [2:0] shamt,
  input  [15:0] in1,
  input  [15:0] in2,
  output ovf,
  output Zero,
  output [15:0] OutputData
);

  wire add, And, Or, shiftLeft, shiftRight, sub;
  wire [15:0] OutAddSub, OutAnd, OutOr, OutShifterLeft, OutShifterRight;

  Decoder #(.select(3), .enable("false")) decoder_1 (
    .out0(add), .out1(sub), .out2(shiftLeft), .out3(shiftRight), .out4(And), .out5(Or), .sel(OpType));  // open: out6, out7
  Multiplexer #(.select(3), .width(16), .enable("false")) multiplexer_1 (
    .in0(OutAddSub), .in1(OutAddSub), .in2(OutShifterLeft), .in3(OutShifterRight), .in4(OutAnd), .in5(OutOr),
    .out(OutputData), .sel(OpType));  // open: in6, in7
  fullAdder fulladder_1 (.sub(sub), .ovf(ovf), .result(OutAddSub), .B(in2), .A(in1), .Zero(Zero));
  threeBitShifterLeft threebitshifterleft_1 (.\input (in1), .\output (OutShifterLeft), .bits(shamt));
  // threeBitShifterRight threebitshifterright_1: pin names not known; wires that end beside it: in1, shamt, OutShifterRight
  assign OutAnd = in1 & in2;  // AND_Gate and_1, 16 bits wide
  assign OutOr = in1 | in2;  // OR_Gate or_1, 16 bits wide

  // Other names for the same wires on the sheet: Out[15:0] = OutputData

  // Notes on the sheet:
  //   Add/Subtract
  //   ShifterLeft
  //   ShifterRight
  //   And
  //   Or
endmodule

module fullAdder (
  input  sub,
  input  [15:0] B,
  input  [15:0] A,
  output Zero,
  output [15:0] result,
  output ovf
);

  wire bitfulladder_1_c_out, bitfulladder_2_c_out, bitfulladder_3_c_out, bitfulladder_4_c_out,
       bitfulladder_5_c_out, bitfulladder_6_c_out, bitfulladder_7_c_out, bitfulladder_8_c_out,
       bitfulladder_9_c_out, bitfulladder_10_c_out, bitfulladder_11_c_out, bitfulladder_12_c_out,
       bitfulladder_13_c_out, bitfulladder_14_c_out, bitfulladder_15_c_out, bitfulladder_16_c_out, or_1_out,
       xor_2_out, xor_3_out, xor_4_out, xor_5_out, xor_6_out, xor_7_out, xor_8_out, xor_9_out, xor_10_out,
       xor_11_out, xor_12_out, xor_13_out, xor_14_out, xor_15_out, xor_16_out, xor_17_out;

  xor xor_1 (ovf, bitfulladder_1_c_out, bitfulladder_2_c_out);
  bitFullAdder bitfulladder_1 (
    .a(A[15]), .b(xor_2_out), .sum(result[15]), .c_in(bitfulladder_2_c_out), .c_out(bitfulladder_1_c_out));
  xor xor_2 (xor_2_out, sub, B[15]);
  bitFullAdder bitfulladder_2 (
    .a(A[14]), .b(xor_3_out), .sum(result[14]), .c_in(bitfulladder_3_c_out), .c_out(bitfulladder_2_c_out));
  xor xor_3 (xor_3_out, sub, B[14]);
  bitFullAdder bitfulladder_3 (
    .a(A[13]), .b(xor_4_out), .sum(result[13]), .c_in(bitfulladder_4_c_out), .c_out(bitfulladder_3_c_out));
  xor xor_4 (xor_4_out, sub, B[13]);
  bitFullAdder bitfulladder_4 (
    .a(A[12]), .b(xor_5_out), .sum(result[12]), .c_in(bitfulladder_5_c_out), .c_out(bitfulladder_4_c_out));
  xor xor_5 (xor_5_out, sub, B[12]);
  bitFullAdder bitfulladder_5 (
    .a(A[11]), .b(xor_6_out), .sum(result[11]), .c_in(bitfulladder_6_c_out), .c_out(bitfulladder_5_c_out));
  xor xor_6 (xor_6_out, sub, B[11]);
  not not_1 (Zero, or_1_out);
  or or_1 (or_1_out, result[0], result[1], result[2], result[3], result[4], result[5], result[6], result[7], result[9], result[10], result[11], result[12], result[13], result[14], result[15], result[8]);
  bitFullAdder bitfulladder_6 (
    .a(A[10]), .b(xor_7_out), .sum(result[10]), .c_in(bitfulladder_7_c_out), .c_out(bitfulladder_6_c_out));
  xor xor_7 (xor_7_out, sub, B[10]);
  bitFullAdder bitfulladder_7 (
    .a(A[9]), .b(xor_8_out), .sum(result[9]), .c_in(bitfulladder_8_c_out), .c_out(bitfulladder_7_c_out));
  xor xor_8 (xor_8_out, sub, B[9]);
  bitFullAdder bitfulladder_8 (
    .a(A[8]), .b(xor_9_out), .sum(result[8]), .c_in(bitfulladder_9_c_out), .c_out(bitfulladder_8_c_out));
  xor xor_9 (xor_9_out, sub, B[8]);
  bitFullAdder bitfulladder_9 (
    .a(A[7]), .b(xor_10_out), .sum(result[7]), .c_in(bitfulladder_10_c_out), .c_out(bitfulladder_9_c_out));
  xor xor_10 (xor_10_out, sub, B[7]);
  bitFullAdder bitfulladder_10 (
    .a(A[6]), .b(xor_11_out), .sum(result[6]), .c_in(bitfulladder_11_c_out), .c_out(bitfulladder_10_c_out));
  xor xor_11 (xor_11_out, sub, B[6]);
  bitFullAdder bitfulladder_11 (
    .a(A[5]), .b(xor_12_out), .sum(result[5]), .c_in(bitfulladder_12_c_out), .c_out(bitfulladder_11_c_out));
  xor xor_12 (xor_12_out, sub, B[5]);
  bitFullAdder bitfulladder_12 (
    .a(A[4]), .b(xor_13_out), .sum(result[4]), .c_in(bitfulladder_13_c_out), .c_out(bitfulladder_12_c_out));
  xor xor_13 (xor_13_out, sub, B[4]);
  bitFullAdder bitfulladder_13 (
    .a(A[3]), .b(xor_14_out), .sum(result[3]), .c_in(bitfulladder_14_c_out), .c_out(bitfulladder_13_c_out));
  xor xor_14 (xor_14_out, sub, B[3]);
  bitFullAdder bitfulladder_14 (
    .a(A[2]), .b(xor_15_out), .sum(result[2]), .c_in(bitfulladder_15_c_out), .c_out(bitfulladder_14_c_out));
  xor xor_15 (xor_15_out, sub, B[2]);
  bitFullAdder bitfulladder_15 (
    .a(A[1]), .b(xor_16_out), .sum(result[1]), .c_in(bitfulladder_16_c_out), .c_out(bitfulladder_15_c_out));
  xor xor_16 (xor_16_out, sub, B[1]);
  bitFullAdder bitfulladder_16 (.a(A[0]), .b(xor_17_out), .sum(result[0]), .c_in(sub), .c_out(bitfulladder_16_c_out));
  xor xor_17 (xor_17_out, sub, B[0]);

  // Other names for the same wires on the sheet: a_t[15:0] = A; b_t[15:0] = B
endmodule

module bitFullAdder (
  input  c_in,
  input  a,
  input  b,
  output sum,
  output c_out
);

  wire and_1_out, and_2_out, xor_1_out;

  and and_1 (and_1_out, b, a);
  or or_1 (c_out, and_1_out, and_2_out);
  xor xor_1 (xor_1_out, a, b);
  and and_2 (and_2_out, xor_1_out, c_in);
  xor xor_2 (sum, c_in, xor_1_out);
endmodule

module threeBitShifterLeft (
  input  [15:0] \input ,
  input  [2:0] bits,
  output [15:0] \output 
);

  wire [15:0] twobitshifterleft_1_output;

  twoBitShifterLeft twobitshifterleft_1 (.\input (\input ), .\output (twobitshifterleft_1_output), .bits(bits[1:0]));
  Multiplexer #(.enable("false")) multiplexer_1 (
    .in0(twobitshifterleft_1_output[0]), .in1(1'b0), .out(\output [0]), .sel(bits[2]));
  Multiplexer #(.enable("false")) multiplexer_2 (
    .in0(twobitshifterleft_1_output[1]), .in1(1'b0), .out(\output [1]), .sel(bits[2]));
  Multiplexer #(.enable("false")) multiplexer_3 (
    .in0(twobitshifterleft_1_output[2]), .in1(1'b0), .out(\output [2]), .sel(bits[2]));
  Multiplexer #(.enable("false")) multiplexer_4 (
    .in0(twobitshifterleft_1_output[3]), .in1(1'b0), .out(\output [3]), .sel(bits[2]));
  Multiplexer #(.enable("false")) multiplexer_5 (
    .in0(twobitshifterleft_1_output[4]), .in1(twobitshifterleft_1_output[0]), .out(\output [4]), .sel(bits[2]));
  Multiplexer #(.enable("false")) multiplexer_6 (
    .in0(twobitshifterleft_1_output[5]), .in1(twobitshifterleft_1_output[1]), .out(\output [5]), .sel(bits[2]));
  Multiplexer #(.enable("false")) multiplexer_7 (
    .in0(twobitshifterleft_1_output[6]), .in1(twobitshifterleft_1_output[2]), .out(\output [6]), .sel(bits[2]));
  Multiplexer #(.enable("false")) multiplexer_8 (
    .in0(twobitshifterleft_1_output[7]), .in1(twobitshifterleft_1_output[3]), .out(\output [7]), .sel(bits[2]));
  Multiplexer #(.enable("false")) multiplexer_9 (
    .in0(twobitshifterleft_1_output[8]), .in1(twobitshifterleft_1_output[4]), .out(\output [8]), .sel(bits[2]));
  Multiplexer #(.enable("false")) multiplexer_10 (
    .in0(twobitshifterleft_1_output[9]), .in1(twobitshifterleft_1_output[5]), .out(\output [9]), .sel(bits[2]));
  Multiplexer #(.enable("false")) multiplexer_11 (
    .in0(twobitshifterleft_1_output[10]), .in1(twobitshifterleft_1_output[6]), .out(\output [10]),
    .sel(bits[2]));
  Multiplexer #(.enable("false")) multiplexer_12 (
    .in0(twobitshifterleft_1_output[11]), .in1(twobitshifterleft_1_output[7]), .out(\output [11]),
    .sel(bits[2]));
  Multiplexer #(.enable("false")) multiplexer_13 (
    .in0(twobitshifterleft_1_output[12]), .in1(twobitshifterleft_1_output[8]), .out(\output [12]),
    .sel(bits[2]));
  Multiplexer #(.enable("false")) multiplexer_14 (
    .in0(twobitshifterleft_1_output[13]), .in1(twobitshifterleft_1_output[9]), .out(\output [13]),
    .sel(bits[2]));
  Multiplexer #(.enable("false")) multiplexer_15 (
    .in0(twobitshifterleft_1_output[14]), .in1(twobitshifterleft_1_output[10]), .out(\output [14]),
    .sel(bits[2]));
  Multiplexer #(.enable("false")) multiplexer_16 (
    .in0(twobitshifterleft_1_output[15]), .in1(twobitshifterleft_1_output[11]), .out(\output [15]),
    .sel(bits[2]));

  // Other names for the same wires on the sheet: bit0 = bits[0]; bit1 = bits[1]; bit2 = bits[2]; in[15:0] = \input ;
  //   out[15:0] = \output 
endmodule

module twoBitShifterLeft (
  input  [15:0] \input ,
  input  [1:0] bits,
  output [15:0] \output 
);

  wire [15:0] bitshifterleft_1_output;

  bitShifterLeft bitshifterleft_1 (.\input (\input ), .\output (bitshifterleft_1_output), .shift(bits[0]));
  Multiplexer #(.enable("false")) multiplexer_1 (
    .in0(bitshifterleft_1_output[0]), .in1(1'b0), .out(\output [0]), .sel(bits[1]));
  Multiplexer #(.enable("false")) multiplexer_2 (
    .in0(bitshifterleft_1_output[1]), .in1(1'b0), .out(\output [1]), .sel(bits[1]));
  Multiplexer #(.enable("false")) multiplexer_3 (
    .in0(bitshifterleft_1_output[2]), .in1(bitshifterleft_1_output[0]), .out(\output [2]), .sel(bits[1]));
  Multiplexer #(.enable("false")) multiplexer_4 (
    .in0(bitshifterleft_1_output[3]), .in1(bitshifterleft_1_output[1]), .out(\output [3]), .sel(bits[1]));
  Multiplexer #(.enable("false")) multiplexer_5 (
    .in0(bitshifterleft_1_output[4]), .in1(bitshifterleft_1_output[2]), .out(\output [4]), .sel(bits[1]));
  Multiplexer #(.enable("false")) multiplexer_6 (
    .in0(bitshifterleft_1_output[5]), .in1(bitshifterleft_1_output[3]), .out(\output [5]), .sel(bits[1]));
  Multiplexer #(.enable("false")) multiplexer_7 (
    .in0(bitshifterleft_1_output[6]), .in1(bitshifterleft_1_output[4]), .out(\output [6]), .sel(bits[1]));
  Multiplexer #(.enable("false")) multiplexer_8 (
    .in0(bitshifterleft_1_output[7]), .in1(bitshifterleft_1_output[5]), .out(\output [7]), .sel(bits[1]));
  Multiplexer #(.enable("false")) multiplexer_9 (
    .in0(bitshifterleft_1_output[8]), .in1(bitshifterleft_1_output[6]), .out(\output [8]), .sel(bits[1]));
  Multiplexer #(.enable("false")) multiplexer_10 (
    .in0(bitshifterleft_1_output[9]), .in1(bitshifterleft_1_output[7]), .out(\output [9]), .sel(bits[1]));
  Multiplexer #(.enable("false")) multiplexer_11 (
    .in0(bitshifterleft_1_output[10]), .in1(bitshifterleft_1_output[8]), .out(\output [10]), .sel(bits[1]));
  Multiplexer #(.enable("false")) multiplexer_12 (
    .in0(bitshifterleft_1_output[11]), .in1(bitshifterleft_1_output[9]), .out(\output [11]), .sel(bits[1]));
  Multiplexer #(.enable("false")) multiplexer_13 (
    .in0(bitshifterleft_1_output[12]), .in1(bitshifterleft_1_output[10]), .out(\output [12]), .sel(bits[1]));
  Multiplexer #(.enable("false")) multiplexer_14 (
    .in0(bitshifterleft_1_output[13]), .in1(bitshifterleft_1_output[11]), .out(\output [13]), .sel(bits[1]));
  Multiplexer #(.enable("false")) multiplexer_15 (
    .in0(bitshifterleft_1_output[14]), .in1(bitshifterleft_1_output[12]), .out(\output [14]), .sel(bits[1]));
  Multiplexer #(.enable("false")) multiplexer_16 (
    .in0(bitshifterleft_1_output[15]), .in1(bitshifterleft_1_output[13]), .out(\output [15]), .sel(bits[1]));

  // Other names for the same wires on the sheet: bit0 = bits[0]; bit1 = bits[1]; in[15:0] = \input ;
  //   out[15:0] = \output 
endmodule

module bitShifterLeft (
  input  [15:0] \input ,
  input  shift,
  output [15:0] \output 
);

  Multiplexer #(.enable("false")) multiplexer_1 (.in0(\input [0]), .in1(1'b0), .out(\output [0]), .sel(shift));
  Multiplexer #(.enable("false")) multiplexer_2 (.in0(\input [1]), .in1(\input [0]), .out(\output [1]), .sel(shift));
  Multiplexer #(.enable("false")) multiplexer_3 (.in0(\input [2]), .in1(\input [1]), .out(\output [2]), .sel(shift));
  Multiplexer #(.enable("false")) multiplexer_4 (.in0(\input [3]), .in1(\input [2]), .out(\output [3]), .sel(shift));
  Multiplexer #(.enable("false")) multiplexer_5 (.in0(\input [4]), .in1(\input [3]), .out(\output [4]), .sel(shift));
  Multiplexer #(.enable("false")) multiplexer_6 (.in0(\input [5]), .in1(\input [4]), .out(\output [5]), .sel(shift));
  Multiplexer #(.enable("false")) multiplexer_7 (.in0(\input [6]), .in1(\input [5]), .out(\output [6]), .sel(shift));
  Multiplexer #(.enable("false")) multiplexer_8 (.in0(\input [7]), .in1(\input [6]), .out(\output [7]), .sel(shift));
  Multiplexer #(.enable("false")) multiplexer_9 (.in0(\input [8]), .in1(\input [7]), .out(\output [8]), .sel(shift));
  Multiplexer #(.enable("false")) multiplexer_10 (.in0(\input [9]), .in1(\input [8]), .out(\output [9]), .sel(shift));
  Multiplexer #(.enable("false")) multiplexer_11 (.in0(\input [10]), .in1(\input [9]), .out(\output [10]), .sel(shift));
  Multiplexer #(.enable("false")) multiplexer_12 (
    .in0(\input [11]), .in1(\input [10]), .out(\output [11]), .sel(shift));
  Multiplexer #(.enable("false")) multiplexer_13 (
    .in0(\input [12]), .in1(\input [11]), .out(\output [12]), .sel(shift));
  Multiplexer #(.enable("false")) multiplexer_14 (
    .in0(\input [13]), .in1(\input [12]), .out(\output [13]), .sel(shift));
  Multiplexer #(.enable("false")) multiplexer_15 (
    .in0(\input [14]), .in1(\input [13]), .out(\output [14]), .sel(shift));
  Multiplexer #(.enable("false")) multiplexer_16 (
    .in0(\input [15]), .in1(\input [14]), .out(\output [15]), .sel(shift));

  // Other names for the same wires on the sheet: bit0 = shift; in[15:0] = \input ; out[15:0] = \output 
endmodule

module threeBitShifterRight (
  input  [15:0] \input ,
  input  [2:0] bits,
  output [15:0] \output 
);

  threeBitShifterLeft threebitshifterleft_1 (
    .\input ({\input [0], \input [1], \input [2], \input [3], \input [4], \input [5], \input [6], \input [7], \input [8], \input [9], \input [10], \input [11], \input [12], \input [13], \input [14], \input [15]}),
    .\output ({\output [0], \output [1], \output [2], \output [3], \output [4], \output [5], \output [6], \output [7], \output [8], \output [9], \output [10], \output [11], \output [12], \output [13], \output [14], \output [15]}),
    .bits(bits));
endmodule

module register (
  input  WE,
  input  clock,
  input  reset,
  input  [15:0] dataInput,
  output [15:0] \output 
);

  wire not_1_out, write;

  assign write = WE ? clock : 1'bz;  // Controlled_Buffer controlled_buffer_1
  not not_1 (not_1_out, WE);
  assign write = not_1_out ? 1'b0 : 1'bz;  // Controlled_Buffer controlled_buffer_2
  // AND_Gate and_1 has open pins: in0=WE, in1=clock, out=open
  D_Flip_Flop #(.trigger("falling")) d_ff_1 (
    .D(dataInput[0]), .clk(write), .Q(\output [0]), .reset(reset));  // open: Qn, preset
  D_Flip_Flop #(.trigger("falling")) d_ff_2 (
    .D(dataInput[1]), .clk(write), .Q(\output [1]), .reset(reset));  // open: Qn, preset
  D_Flip_Flop #(.trigger("falling")) d_ff_3 (
    .D(dataInput[2]), .clk(write), .Q(\output [2]), .reset(reset));  // open: Qn, preset
  D_Flip_Flop #(.trigger("falling")) d_ff_4 (
    .D(dataInput[3]), .clk(write), .Q(\output [3]), .reset(reset));  // open: Qn, preset
  D_Flip_Flop #(.trigger("falling")) d_ff_5 (
    .D(dataInput[4]), .clk(write), .Q(\output [4]), .reset(reset));  // open: Qn, preset
  D_Flip_Flop #(.trigger("falling")) d_ff_6 (
    .D(dataInput[5]), .clk(write), .Q(\output [5]), .reset(reset));  // open: Qn, preset
  D_Flip_Flop #(.trigger("falling")) d_ff_7 (
    .D(dataInput[6]), .clk(write), .Q(\output [6]), .reset(reset));  // open: Qn, preset
  D_Flip_Flop #(.trigger("falling")) d_ff_8 (
    .D(dataInput[7]), .clk(write), .Q(\output [7]), .reset(reset));  // open: Qn, preset
  D_Flip_Flop #(.trigger("falling")) d_ff_9 (
    .D(dataInput[8]), .clk(write), .Q(\output [8]), .reset(reset));  // open: Qn, preset
  D_Flip_Flop #(.trigger("falling")) d_ff_10 (
    .D(dataInput[9]), .clk(write), .Q(\output [9]), .reset(reset));  // open: Qn, preset
  D_Flip_Flop #(.trigger("falling")) d_ff_11 (
    .D(dataInput[10]), .clk(write), .Q(\output [10]), .reset(reset));  // open: Qn, preset
  D_Flip_Flop #(.trigger("falling")) d_ff_12 (
    .D(dataInput[11]), .clk(write), .Q(\output [11]), .reset(reset));  // open: Qn, preset
  D_Flip_Flop #(.trigger("falling")) d_ff_13 (
    .D(dataInput[12]), .clk(write), .Q(\output [12]), .reset(reset));  // open: Qn, preset
  D_Flip_Flop #(.trigger("falling")) d_ff_14 (
    .D(dataInput[13]), .clk(write), .Q(\output [13]), .reset(reset));  // open: Qn, preset
  D_Flip_Flop #(.trigger("falling")) d_ff_15 (
    .D(dataInput[14]), .clk(write), .Q(\output [14]), .reset(reset));  // open: Qn, preset
  D_Flip_Flop #(.trigger("falling")) d_ff_16 (
    .D(dataInput[15]), .clk(write), .Q(\output [15]), .reset(reset));  // open: Qn, preset
endmodule

module instructionDecoder (
  input  [3:0] opcode,
  output Rwe,
  output Rdst,
  output [2:0] ALUOp,
  output ALUinB,
  output Rwd,
  output DMwe,
  output BEQ,
  output BLT,
  output JP,
  output OUTPUT,
  output INPUT
);

  wire add, addi, \and , j, jal, \or , shl, shr, sub, subi;

  or or_1 (ALUOp[2], \and , \or );
  or or_2 (ALUOp[1], shr, shl);
  Decoder #(.select(4), .enable("false")) decoder_1 (
    .out0(Rwd), .out1(DMwe), .out2(BEQ), .out3(BLT), .out4(\or ), .out5(\and ), .out6(addi), .out7(add),
    .out8(sub), .out9(subi), .out10(shr), .out11(shl), .out12(j), .out13(jal), .out14(OUTPUT), .out15(INPUT),
    .sel(opcode));
  or or_3 (ALUOp[0], shr, subi, sub, \or , BLT, BEQ);
  or or_4 (JP, j, jal);
  or or_5 (ALUinB, Rwd, addi, subi, DMwe);
  or or_6 (Rwe, \or , Rwd, addi, add, sub, subi, shr, shl, jal, INPUT, \and );
  or or_7 (Rdst, \or , \and , add, sub, shr, shl, INPUT);

  // Other names for the same wires on the sheet: lw = Rwd; sw = DMwe
endmodule

module RegisterFile (
  input  WE,
  input  clk,
  input  reset,
  input  [15:0] RDVAL,
  input  [2:0] RD,
  input  [2:0] RS1,
  input  [2:0] RS2,
  output [15:0] RS1VAL,
  output [15:0] RS2VAL
);

  wire and_1_out, and_2_out, and_3_out, and_4_out, and_5_out, and_6_out, and_7_out, and_8_out, RD_r0, RD_r1,
       RD_r2, RD_r3, RD_r4, RD_r5, RD_r6, RD_r7;
  wire [15:0] register_1_output, register_2_output, register_3_output, register_4_output, register_5_output,
       register_6_output, register_7_output, register_8_output;

  Decoder #(.select(3), .enable("false")) decoder_1 (
    .out0(RD_r0), .out1(RD_r1), .out2(RD_r2), .out3(RD_r3), .out4(RD_r4), .out5(RD_r5), .out6(RD_r6),
    .out7(RD_r7), .sel(RD));
  and and_1 (and_1_out, RD_r0, WE);
  and and_2 (and_2_out, RD_r1, WE);
  and and_3 (and_3_out, RD_r2, WE);
  and and_4 (and_4_out, RD_r3, WE);
  and and_5 (and_5_out, RD_r4, WE);
  and and_6 (and_6_out, RD_r5, WE);
  and and_7 (and_7_out, RD_r6, WE);
  and and_8 (and_8_out, RD_r7, WE);
  register register_1 (
    .WE(and_1_out), .reset(reset), .dataInput({16{1'b0}}), .\output (register_1_output), .clock(clk));
  register register_2 (.WE(and_2_out), .reset(reset), .dataInput(RDVAL), .\output (register_2_output), .clock(clk));
  register register_3 (.WE(and_3_out), .reset(reset), .dataInput(RDVAL), .\output (register_3_output), .clock(clk));
  register register_4 (.WE(and_4_out), .reset(reset), .dataInput(RDVAL), .\output (register_4_output), .clock(clk));
  register register_5 (.WE(and_5_out), .reset(reset), .dataInput(RDVAL), .\output (register_5_output), .clock(clk));
  register register_6 (.WE(and_6_out), .reset(reset), .dataInput(RDVAL), .\output (register_6_output), .clock(clk));
  register register_7 (.WE(and_7_out), .reset(reset), .dataInput(RDVAL), .\output (register_7_output), .clock(clk));
  register register_8 (.WE(and_8_out), .reset(reset), .dataInput(RDVAL), .\output (register_8_output), .clock(clk));
  // Probe on register_1_output
  // Probe on register_2_output
  // Probe on register_3_output
  // Probe on register_4_output
  // Probe on register_5_output
  // Probe on register_6_output
  // Probe on register_7_output
  // Probe on register_8_output
  Multiplexer #(.select(3), .width(16), .enable("false")) multiplexer_1 (
    .in0(register_1_output), .in1(register_2_output), .in2(register_3_output), .in3(register_4_output),
    .in4(register_5_output), .in5(register_6_output), .in6(register_7_output), .in7(register_8_output),
    .out(RS2VAL), .sel(RS2));
  Multiplexer #(.select(3), .width(16), .enable("false")) multiplexer_2 (
    .in0(register_1_output), .in1(register_2_output), .in2(register_3_output), .in3(register_4_output),
    .in4(register_5_output), .in5(register_6_output), .in6(register_7_output), .in7(register_8_output),
    .out(RS1VAL), .sel(RS1));
endmodule

module signExtender (
  input  [5:0] \input ,
  output [15:0] \output 
);

  Multiplexer #(.width(10), .enable("false")) multiplexer_1 (
    .in0({10{1'b0}}), .in1({10{1'b1}}), .out(\output [15:6]), .sel(\input [5]));

  assign \output [5:0] = \input ;

  // Other names for the same wires on the sheet: neg = \input [5]
endmodule

module memoryLatch (
  input  [15:0] address,
  input  WE,
  input  clk,
  input  [15:0] data_in,
  output [15:0] address_latched,
  output WE_latched,
  output OE_latched,
  output [15:0] data_in_latched
);

  wire d_ff_1_q;
  wire [15:0] register_1_q;

  Register #(.width(16), .trigger("falling")) register_1 (
    .D(address), .en(WE), .clk(clk), .Q(register_1_q));  // open: clr
  D_Flip_Flop #(.trigger("falling")) d_ff_1 (.D(WE), .clk(clk), .Q(d_ff_1_q));  // open: Qn, preset, reset
  Register #(.width(16), .trigger("falling")) register_2 (
    .D(data_in), .en(WE), .clk(clk), .Q(data_in_latched));  // open: clr
  Multiplexer #(.width(16), .enable("false")) multiplexer_1 (
    .in0(address), .in1(register_1_q), .out(address_latched), .sel(d_ff_1_q));
  and and_1 (WE_latched, clk, d_ff_1_q);
  not not_1 (OE_latched, WE_latched);
endmodule
